// Logisim project Extra.circ as structural Verilog: 22 circuits, main circuit OneLogic
module main (
);

  wire and_1_out, clock_1_out, comparator_1_eq, comparator_2_eq, d_ff_1_q, digitdetector_1_digitfound,
       FoundFirst_q, not_1_out, or_1_out;
  wire [7:0] rom_1_data;
  wire [15:0] adder_1_out, adder_2_out, counter_1_q, digitdetector_1_value, FirstDigit_q, LastDigit_q,
       multiplier_1_out, register_1_q;

  Clock clock_1 (.out(clock_1_out));
  ROM #(.addrWidth(16)) rom_1 (.addr(counter_1_q), .data(rom_1_data));
  Counter #(.max('hffff), .ongoal("stay"), .width(16)) counter_1 (
    .Q(counter_1_q), .clk(and_1_out));  // open: load, D, count, carry, up, clr
  and and_1 (and_1_out, clock_1_out, ~comparator_2_eq);  // AND_Gate
  Comparator comparator_1 (.a(rom_1_data), .b(8'hd), .eq(comparator_1_eq));  // open: gt, lt
  Comparator comparator_2 (.a(rom_1_data), .b({8{1'b0}}), .eq(comparator_2_eq));  // open: gt, lt
  D_Flip_Flop d_ff_1 (.D(comparator_1_eq), .clk(and_1_out), .Q(d_ff_1_q));  // open: Qn, preset, reset
  DigitDetector digitdetector_1 (
    .char(rom_1_data), .clock(and_1_out), .value(digitdetector_1_value),
    .DigitFound(digitdetector_1_digitfound));
  Register #(.width(1)) FoundFirst (.D(or_1_out), .clk(and_1_out), .Q(FoundFirst_q), .clr(d_ff_1_q));  // open: en
  or or_1 (or_1_out, FoundFirst_q, digitdetector_1_digitfound);
  not not_1 (not_1_out, FoundFirst_q);
  Register #(.width(16)) FirstDigit (
    .D(digitdetector_1_value), .en(not_1_out), .clk(and_1_out), .Q(FirstDigit_q), .clr(d_ff_1_q));
  Register #(.width(16)) LastDigit (
    .D(digitdetector_1_value), .en(digitdetector_1_digitfound), .clk(and_1_out), .Q(LastDigit_q),
    .clr(d_ff_1_q));
  Multiplier #(.width(16)) multiplier_1 (.a(FirstDigit_q), .b(16'ha), .out(multiplier_1_out));  // open: cin, cout
  // Probe on adder_1_out
  Adder #(.width(16)) adder_1 (.a(multiplier_1_out), .b(LastDigit_q), .out(adder_1_out));  // open: cin, cout
  Register #(.width(16)) register_1 (
    .D(adder_2_out), .en(comparator_1_eq), .clk(and_1_out), .Q(register_1_q));  // open: clr
  Adder #(.width(16)) adder_2 (.a(register_1_q), .b(adder_1_out), .out(adder_2_out));  // open: cin, cout
  // Probe on register_1_q
  LED Done (.in(comparator_2_eq));

  // Notes on the sheet:
  //   contents of rom_1 (hex, n*v repeats v):
  //   39 65 69 67 68 74 6f 6e 65 d a 68 63 7a 73 71 66 6f 75 72 33 6e 78 6d 35 73 65 76 65 6e 34 d a 39 74
  //   77 6f 70 6a 71 6b 67 68 6d 62 6f 6e 65 d a 72 68 72 66 74 68 76 38 38 36 76 66 6c 74 68 72 65 65 7a
  //   74 76 7a 73 d a 74 6c 62 74 77 6f 36 32 66 69 76 65 d a 6e 69 6e 65 74 77 6f 6e 69 6e 65 32 33 34 6e
  //   76 74 6c 7a 78 7a 63 7a 78 d a 32 38 73 65 76 65 6e 73 65 76 65 6e d a 32 73 65 76 65 6e 73 78 73 7a
  //   71 64 68 6a 67 32 74 68 72 65 65 78 7a 6a 6a 33 d a 32 66 76 71 d a 37 38 31 64 6b 39 37 65 69 67 68
  //   74 32 36 d a 70 6c 66 72 73 6a 74 62 6c 36 d a 73 69 78 67 6c 6a 31 33 d a 62 33 73 65 76 65 6e 36
  //   38 31 37 67 6a 70 63 78 73 65 76 65 6e d a 33 66 69 76 65 6e 6c 71 63 62 73 7a 66 6f 75 72 73 69 78
  //   66 69 76 65 36 73 69 78 66 62 d a 7a 66 78 62 7a 68 63 7a 63 78 39 65 69 67 68 74 77 6f 63 6b 6b d a
  //   74 68 72 65 65 64 73 73 71 72 6c 6b 32 71 6e 70 6b 7a 70 6b 64 64 64 74 d a 74 68 72 65 65 36 37 66
  //   6f 75 72 6b 62 72 6c 6b 66 37 6d 74 62 6a 70 72 72 74 68 32 d a 73 65 76 65 6e 33 6f 6e 65 69 67 68
  //   74 70 d a 33 31 74 68 72 65 65 d a 33 38 39 34 73 65 76 65 6e 66 6f 75 72 66 6f 75 72 d a 33 67 68
  //   6d 71 6c 6e 69 6e 65 d a 37 6e 69 6e 65 35 7a 70 6c 68 d a 33 74 68 72 65 65 39 d a 66 66 36 64 68
  //   76 7a 6d 64 72 67 74 d a 33 6f 6e 65 33 66 6f 75 72 d a 66 6f 75 72 76 70 74 64 6e 62 70 71 63 78 6b
  //   74 77 6f 6f 6e 65 34 6f 6e 65 6f 6e 65 d a 64 36 d a 34 6b 74 68 78 32 d a 6b 74 6a 76 72 6d 64 6a
  //   66 32 37 66 69 76 65 38 6f 6e 65 d a 39 34 67 6b 76 6b 67 68 66 6a 71 70 73 69 78 d a 34 67 7a 73 74
  //   66 70 62 71 62 6c 71 6b 78 71 72 76 64 d a 65 69 67 68 74 31 6e 69 6e 65 d a 38 7a 67 70 70 74 6b 71
  //   6a 64 67 6c 70 6b 73 73 62 70 67 7a 6d 6e 38 35 d a 73 69 78 70 6d 66 6a 72 64 6d 63 6a 37 36 d a 73
  //   69 78 39 37 d a 6e 69 6e 65 73 78 73 37 d a 6f 6e 65 35 6c 76 78 70 66 62 6e 6c 66 71 d a 6a 6e 69
  //   6e 65 70 7a 70 67 74 7a 71 37 66 6f 75 72 35 d a 66 6f 75 72 76 6a 6a 72 74 74 6c 76 64 74 66 6f 75
  //   72 38 71 78 64 76 6c 67 32 32 74 77 6f d a 37 70 71 71 64 72 72 76 63 6d 76 62 72 38 6e 69 6e 65 35
  //   37 d a 67 76 73 64 6c 64 71 71 78 74 6a 74 73 6e 6e 68 31 34 37 68 78 66 6f 75 72 d a 35 6e 6e 70 68
  //   31 74 68 72 65 65 d a 66 6b 66 7a 72 64 6a 76 6d 6e 76 39 6f 6e 65 6d 68 6c 73 6a 7a 72 6d 78 7a 7a
  //   6a 66 6f 75 72 6a 6b 76 76 67 6e d a 67 67 78 76 63 70 66 78 6c 70 6a 6e 62 74 6d 70 33 6f 6e 65 63
  //   6d 67 72 d a 74 68 72 65 65 38 72 6a 6d 32 d a 38 38 34 32 34 66 6f 75 72 31 d a 6a 6b 67 6d 63 6d
  //   37 66 6f 75 72 36 33 74 68 72 65 65 d a 39 74 77 6f 74 77 6f 33 d a 73 6b 7a 7a 73 66 76 68 6e 69 6e
  //   65 35 64 67 7a 76 64 7a d a 65 69 67 68 74 37 31 6c 31 67 74 68 72 65 65 d a 73 68 66 72 73 64 73 67
  //   70 73 66 70 71 67 66 6c 76 68 64 68 73 6d 6c 78 76 70 72 71 72 70 6c 70 6d 7a 6e 66 69 76 65 33 32
  //   32 34 d a 32 35 33 36 73 65 76 65 6e 73 65 76 65 6e 6d 71 74 72 6b 7a 6c 66 71 6b 67 70 d a 78 6e 6d
  //   66 69 76 65 38 66 6f 75 72 73 69 78 73 69 78 38 7a 6a 6c 63 7a 71 d a 37 74 68 72 65 65 6b 74 68 72
  //   65 65 d a 68 63 6a 65 69 67 68 74 6f 6e 65 38 34 71 66 6a 71 6b 78 78 68 39 d a 6c 6e 7a 6b 71 66 7a
  //   6d 78 6f 6e 65 66 6f 75 72 71 73 70 6c 76 6a 36 71 74 68 6b 78 34 66 6f 75 72 70 76 72 68 d a 37 36
  //   6f 6e 65 6a 78 74 68 6c 6c 76 78 72 6e 38 32 6c 64 64 78 78 38 36 d a 35 6d 64 67 78 76 70 73 65 76
  //   65 6e 65 69 67 68 74 6b 78 6c 74 6b 6e 6c 7a d a 33 73 69 78 6e 66 6f 75 72 66 6f 75 72 6b 64 70 66
  //   72 67 64 73 6a 68 73 65 76 65 6e 74 68 72 65 65 d a 74 77 6f 37 32 d a 31 37 38 31 6c 63 78 76 67 7a
  //   31 73 69 78 72 6c 78 74 64 68 67 6a d a 74 68 72 65 65 32 6b 78 72 68 6e 76 6b 72 73 76 39 d a 31 62
  //   6b 6c 62 62 6b 64 68 32 73 65 76 65 6e 6a 6b 63 63 6b 72 6b 68 6d d a 34 74 78 64 71 6c 6a 32 71 6a
  //   6a 78 78 6b d a 7a 6e 64 63 64 67 6e 69 6e 65 74 68 72 65 65 6b 64 73 70 7a 73 67 66 35 6e 69 6e 65
  //   74 64 78 d a 32 38 68 6b 76 6e 6c 78 65 69 67 68 74 d a 72 6e 74 6d 64 74 68 72 65 65 6f 6e 65 37 73
  //   69 78 70 72 71 64 74 62 73 71 73 31 32 d a 66 6f 75 72 71 67 62 6b 78 64 6a 39 65 69 67 68 74 74 68
  //   72 65 65 d a 65 69 67 68 74 6e 74 72 6c 71 66 66 78 7a 6a 6a 71 72 78 76 74 68 72 65 65 37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
  //   EndOfLine
  //   EndOfFile
  //   Reset
endmodule

module DigitDetector (
  input  [7:0] char,
  input  clock,
  output [15:0] value,
  output DigitFound
);

  wire eightfsm_1_eight, fivefsm_1_five, fourfsm_1_four, ninefsm_1_nine, onefsm_1_one, sevenfsm_1_seven,
       sixfsm_1_six, threefsm_1_three, twofsm_1_two, zerofsm_1_zero;
  wire [3:0] priority_encoder_1_out;

  ZeroFSM zerofsm_1 (.char(char), .clock(clock), .zero(zerofsm_1_zero));
  OneFSM onefsm_1 (.char(char), .clock(clock), .one(onefsm_1_one));
  TwoFSM twofsm_1 (.char(char), .clock(clock), .two(twofsm_1_two));
  ThreeFSM threefsm_1 (.char(char), .clock(clock), .three(threefsm_1_three));
  FourFSM fourfsm_1 (.char(char), .clock(clock), .four(fourfsm_1_four));
  FiveFSM fivefsm_1 (.char(char), .clock(clock), .five(fivefsm_1_five));
  SixFSM sixfsm_1 (.char(char), .clock(clock), .six(sixfsm_1_six));
  SevenFSM sevenfsm_1 (.char(char), .clock(clock), .seven(sevenfsm_1_seven));
  EightFSM eightfsm_1 (.char(char), .clock(clock), .eight(eightfsm_1_eight));
  NineFSM ninefsm_1 (.char(char), .clock(clock), .nine(ninefsm_1_nine));
  Priority_Encoder #(.select(4)) priority_encoder_1 (
    .in0(zerofsm_1_zero), .in1(onefsm_1_one), .in2(twofsm_1_two), .in3(threefsm_1_three),
    .in4(fourfsm_1_four), .in5(fivefsm_1_five), .in6(sixfsm_1_six), .in7(sevenfsm_1_seven),
    .in8(eightfsm_1_eight), .in9(ninefsm_1_nine), .out(priority_encoder_1_out), .gs(DigitFound));  // open: in10, in11, in12, in13, in14, in15, en_out, en_in
  Pull_Resistor pull_resistor_1 (.node(priority_encoder_1_out));
  assign value = {{12{1'b0}}, priority_encoder_1_out};  // Bit_Extender bit_extender_1
endmodule

module ZeroLogic (
  input  [7:0] char,
  input  [1:0] instate,
  output zero,
  output [1:0] outstate
);

  wire and_1_out, and_2_out, and_3_out, and_4_out, and_5_out, and_6_out, not_1_out, not_2_out, not_3_out,
       not_4_out, not_5_out, not_6_out, not_7_out, not_8_out, not_9_out;

  not not_1 (not_1_out, char[7]);
  not not_2 (not_2_out, char[6]);
  not not_3 (not_3_out, char[4]);
  not not_4 (not_4_out, char[3]);
  not not_5 (not_5_out, char[2]);
  not not_6 (not_6_out, char[1]);
  not not_7 (not_7_out, char[0]);
  not not_8 (not_8_out, instate[1]);
  not not_9 (not_9_out, instate[0]);
  and and_1 (and_1_out, not_1_out, not_2_out, char[5], char[4], not_4_out, not_5_out, not_6_out, not_7_out);
  and and_2 (and_2_out, not_1_out, char[6], char[5], not_3_out, char[3], char[2], char[1], char[0], instate[1], instate[0]);
  and and_3 (and_3_out, not_1_out, char[6], char[5], not_3_out, not_4_out, char[2], not_6_out, char[0], not_8_out, instate[0]);
  and and_4 (and_4_out, not_1_out, char[6], char[5], char[4], not_4_out, not_5_out, char[1], not_7_out, instate[1], not_9_out);
  and and_5 (and_5_out, not_1_out, char[6], char[5], char[4], char[3], not_5_out, char[1], not_7_out);
  and and_6 (and_6_out, not_1_out, char[6], char[5], char[4], not_5_out, char[1], not_7_out, instate[1], not_9_out);
  or or_1 (zero, and_1_out, and_2_out);
  or or_2 (outstate[1], and_3_out, and_4_out);
  or or_3 (outstate[0], and_5_out, and_6_out);
endmodule

module OneLogic (
  input  [7:0] char,
  input  [1:0] instate,
  output one,
  output [1:0] outstate
);

  wire and_1_out, and_2_out, and_4_out, and_5_out, not_1_out, not_2_out, not_3_out, not_4_out, not_5_out,
       not_6_out, not_7_out, not_8_out, not_9_out;

  not not_1 (not_1_out, char[7]);
  not not_2 (not_2_out, char[6]);
  not not_3 (not_3_out, char[4]);
  not not_4 (not_4_out, char[3]);
  not not_5 (not_5_out, char[2]);
  not not_6 (not_6_out, char[1]);
  not not_7 (not_7_out, char[0]);
  not not_8 (not_8_out, instate[1]);
  not not_9 (not_9_out, instate[0]);
  and and_1 (and_1_out, not_1_out, not_2_out, char[5], char[4], not_4_out, not_5_out, not_6_out, char[0]);
  and and_2 (and_2_out, not_1_out, char[6], char[5], not_3_out, not_4_out, char[2], not_6_out, char[0], instate[1], not_9_out);
  and and_3 (outstate[1], not_1_out, char[6], char[5], not_3_out, char[3], char[2], char[1], not_7_out, not_8_out, instate[0]);
  and and_4 (and_4_out, not_1_out, char[6], char[5], not_3_out, char[3], char[2], char[1], char[0], not_8_out);
  and and_5 (and_5_out, not_1_out, char[6], char[5], not_3_out, char[3], char[2], char[1], char[0], not_9_out);
  or or_1 (one, and_1_out, and_2_out);
  or or_2 (outstate[0], and_4_out, and_5_out);
endmodule

module TwoLogic (
  input  [7:0] char,
  input  [1:0] instate,
  output two,
  output [1:0] outstate
);

  wire and_1_out, and_2_out, and_4_out, and_5_out, not_1_out, not_2_out, not_3_out, not_4_out, not_5_out,
       not_6_out, not_7_out, not_8_out, not_9_out;

  not not_1 (not_1_out, char[7]);
  not not_2 (not_2_out, char[6]);
  not not_3 (not_3_out, char[4]);
  not not_4 (not_4_out, char[3]);
  not not_5 (not_5_out, char[2]);
  not not_6 (not_6_out, char[1]);
  not not_7 (not_7_out, char[0]);
  not not_8 (not_8_out, instate[1]);
  not not_9 (not_9_out, instate[0]);
  and and_1 (and_1_out, not_1_out, not_2_out, char[5], char[4], not_4_out, not_5_out, char[1], not_7_out);
  and and_2 (and_2_out, not_1_out, char[6], char[5], not_3_out, char[3], char[2], char[1], char[0], instate[1], not_9_out);
  and and_3 (outstate[1], not_1_out, char[6], char[5], char[4], not_4_out, char[2], char[1], char[0], not_8_out, instate[0]);
  and and_4 (and_4_out, not_1_out, char[6], char[5], char[4], not_4_out, char[2], not_6_out, not_7_out, not_8_out);
  and and_5 (and_5_out, not_1_out, char[6], char[5], char[4], not_4_out, char[2], not_6_out, not_7_out, not_9_out);
  or or_1 (two, and_1_out, and_2_out);
  or or_2 (outstate[0], and_4_out, and_5_out);
endmodule

module ThreeLogic (
  input  [7:0] char,
  input  [2:0] instate,
  output three,
  output [2:0] outstate
);

  wire and_1_out, and_2_out, and_4_out, and_5_out, and_6_out, and_7_out, and_8_out, not_1_out, not_2_out,
       not_3_out, not_4_out, not_5_out, not_6_out, not_7_out, not_8_out, not_9_out, not_10_out;

  not not_1 (not_1_out, char[7]);
  not not_2 (not_2_out, char[6]);
  not not_3 (not_3_out, char[4]);
  not not_4 (not_4_out, char[3]);
  not not_5 (not_5_out, char[2]);
  not not_6 (not_6_out, char[1]);
  not not_7 (not_7_out, char[0]);
  not not_8 (not_8_out, instate[2]);
  not not_9 (not_9_out, instate[1]);
  not not_10 (not_10_out, instate[0]);
  and and_1 (and_1_out, not_1_out, not_2_out, char[5], char[4], not_4_out, not_5_out, char[1], char[0]);
  and and_2 (and_2_out, not_1_out, char[6], char[5], not_3_out, not_4_out, char[2], not_6_out, char[0], instate[2], not_9_out, not_10_out);
  and and_3 (outstate[2], not_1_out, char[6], char[5], not_3_out, not_4_out, char[2], not_6_out, char[0], not_8_out, instate[1], instate[0]);
  and and_4 (and_4_out, not_1_out, char[6], char[5], not_3_out, char[3], not_5_out, not_6_out, not_7_out, not_8_out, not_9_out, instate[0]);
  and and_5 (and_5_out, not_1_out, char[6], char[5], char[4], not_4_out, not_5_out, char[1], not_7_out, not_8_out, instate[1], not_10_out);
  and and_6 (and_6_out, not_1_out, char[6], char[5], char[4], not_4_out, char[2], not_6_out, not_7_out, not_8_out);
  and and_7 (and_7_out, not_1_out, char[6], char[5], char[4], not_4_out, not_5_out, char[1], not_7_out, not_8_out, instate[1], not_10_out);
  and and_8 (and_8_out, not_1_out, char[6], char[5], char[4], not_4_out, char[2], not_6_out, not_7_out, not_9_out, not_10_out);
  or or_1 (three, and_1_out, and_2_out);
  or or_2 (outstate[1], and_4_out, and_5_out);
  or or_3 (outstate[0], and_6_out, and_7_out, and_8_out);
endmodule

module FourLogic (
  input  [7:0] char,
  input  [1:0] instate,
  output four,
  output [1:0] outstate
);

  wire and_1_out, and_2_out, and_3_out, and_4_out, and_5_out, and_6_out, not_1_out, not_2_out, not_3_out,
       not_4_out, not_5_out, not_6_out, not_7_out, not_8_out, not_9_out;

  not not_1 (not_1_out, char[7]);
  not not_2 (not_2_out, char[6]);
  not not_3 (not_3_out, char[4]);
  not not_4 (not_4_out, char[3]);
  not not_5 (not_5_out, char[2]);
  not not_6 (not_6_out, char[1]);
  not not_7 (not_7_out, char[0]);
  not not_8 (not_8_out, instate[1]);
  not not_9 (not_9_out, instate[0]);
  and and_1 (and_1_out, not_1_out, not_2_out, char[5], char[4], not_4_out, char[2], not_6_out, not_7_out);
  and and_2 (and_2_out, not_1_out, char[6], char[5], char[4], not_4_out, not_5_out, char[1], not_7_out, instate[1], instate[0]);
  and and_3 (and_3_out, not_1_out, char[6], char[5], char[4], not_4_out, char[2], not_6_out, char[0], instate[1], not_9_out);
  and and_4 (and_4_out, not_1_out, char[6], char[5], not_3_out, char[3], char[2], char[1], char[0], not_8_out, instate[0]);
  and and_5 (and_5_out, not_1_out, char[6], char[5], char[4], not_4_out, char[2], not_6_out, char[0], instate[1], not_9_out);
  and and_6 (and_6_out, not_1_out, char[6], char[5], not_3_out, not_4_out, char[2], char[1], not_7_out);
  or or_1 (four, and_1_out, and_2_out);
  or or_2 (outstate[1], and_3_out, and_4_out);
  or or_3 (outstate[0], and_5_out, and_6_out);
endmodule

module FiveLogic (
  input  [7:0] char,
  input  [1:0] instate,
  output five,
  output [1:0] outstate
);

  wire and_1_out, and_2_out, and_3_out, and_4_out, and_5_out, and_6_out, not_1_out, not_2_out, not_3_out,
       not_4_out, not_5_out, not_6_out, not_7_out, not_8_out, not_9_out;

  not not_1 (not_1_out, char[7]);
  not not_2 (not_2_out, char[6]);
  not not_3 (not_3_out, char[4]);
  not not_4 (not_4_out, char[3]);
  not not_5 (not_5_out, char[2]);
  not not_6 (not_6_out, char[1]);
  not not_7 (not_7_out, char[0]);
  not not_8 (not_8_out, instate[1]);
  not not_9 (not_9_out, instate[0]);
  and and_1 (and_1_out, not_1_out, not_2_out, char[5], char[4], not_4_out, char[2], not_6_out, char[0]);
  and and_2 (and_2_out, not_1_out, char[6], char[5], not_3_out, not_4_out, char[2], not_6_out, char[0], instate[1], instate[0]);
  and and_3 (and_3_out, not_1_out, char[6], char[5], not_3_out, char[3], not_5_out, not_6_out, char[0], not_8_out, instate[0]);
  and and_4 (and_4_out, not_1_out, char[6], char[5], char[4], not_4_out, char[2], char[1], not_7_out, instate[1], not_9_out);
  and and_5 (and_5_out, not_1_out, char[6], char[5], not_3_out, not_4_out, char[2], char[1], not_7_out);
  and and_6 (and_6_out, not_1_out, char[6], char[5], not_4_out, char[2], char[1], not_7_out, instate[1], not_9_out);
  or or_1 (five, and_1_out, and_2_out);
  or or_2 (outstate[1], and_3_out, and_4_out);
  or or_3 (outstate[0], and_5_out, and_6_out);
endmodule

module SixLogic (
  input  [7:0] char,
  input  [1:0] instate,
  output six,
  output [1:0] outstate
);

  wire and_1_out, and_2_out, and_4_out, and_5_out, not_1_out, not_2_out, not_3_out, not_4_out, not_5_out,
       not_6_out, not_7_out, not_8_out, not_9_out;

  not not_1 (not_1_out, char[7]);
  not not_2 (not_2_out, char[6]);
  not not_3 (not_3_out, char[4]);
  not not_4 (not_4_out, char[3]);
  not not_5 (not_5_out, char[2]);
  not not_6 (not_6_out, char[1]);
  not not_7 (not_7_out, char[0]);
  not not_8 (not_8_out, instate[1]);
  not not_9 (not_9_out, instate[0]);
  and and_1 (and_1_out, not_1_out, char[6], char[5], char[4], char[3], not_5_out, not_6_out, not_7_out, instate[1], not_9_out);
  and and_2 (and_2_out, not_1_out, not_2_out, char[5], char[4], not_4_out, char[2], char[1], not_7_out);
  and and_3 (outstate[1], not_1_out, char[6], char[5], not_3_out, char[3], not_5_out, not_6_out, char[0], not_8_out, instate[0]);
  and and_4 (and_4_out, not_1_out, char[6], char[5], char[4], not_4_out, not_5_out, char[1], char[0], not_8_out);
  and and_5 (and_5_out, not_1_out, char[6], char[5], char[4], not_4_out, not_5_out, char[1], char[0], not_9_out);
  or or_1 (six, and_1_out, and_2_out);
  or or_2 (outstate[0], and_4_out, and_5_out);
endmodule

module SevenLogic (
  input  [7:0] char,
  input  [2:0] instate,
  output seven,
  output [2:0] outstate
);

  wire and_1_out, and_2_out, and_4_out, and_5_out, and_6_out, and_7_out, and_8_out, not_1_out, not_2_out,
       not_3_out, not_4_out, not_5_out, not_6_out, not_7_out, not_8_out, not_9_out, not_10_out;

  not not_1 (not_1_out, char[7]);
  not not_2 (not_2_out, char[6]);
  not not_3 (not_3_out, char[4]);
  not not_4 (not_4_out, char[3]);
  not not_5 (not_5_out, char[2]);
  not not_6 (not_6_out, char[1]);
  not not_7 (not_7_out, char[0]);
  not not_8 (not_8_out, instate[2]);
  not not_9 (not_9_out, instate[1]);
  not not_10 (not_10_out, instate[0]);
  and and_1 (and_1_out, not_1_out, char[6], char[5], not_3_out, char[3], char[2], char[1], not_7_out, instate[2], not_9_out, not_10_out);
  and and_2 (and_2_out, not_1_out, not_2_out, char[5], char[4], not_4_out, char[2], char[1], char[0]);
  and and_3 (outstate[2], not_1_out, char[6], char[5], not_3_out, not_4_out, char[2], not_6_out, char[0], not_8_out, instate[1], instate[0]);
  and and_4 (and_4_out, not_1_out, char[6], char[5], char[4], not_4_out, char[2], char[1], not_7_out, not_8_out, instate[1], not_10_out);
  and and_5 (and_5_out, not_1_out, char[6], char[5], not_3_out, not_4_out, char[2], not_6_out, char[0], not_8_out, not_9_out, instate[0]);
  and and_6 (and_6_out, not_1_out, char[6], char[5], char[4], not_4_out, char[2], char[1], not_7_out, not_8_out, instate[1], not_10_out);
  and and_7 (and_7_out, not_1_out, char[6], char[5], char[4], not_4_out, not_5_out, char[1], char[0], not_8_out);
  and and_8 (and_8_out, not_1_out, char[6], char[5], char[4], not_4_out, not_5_out, char[1], char[0], not_9_out, not_10_out);
  or or_1 (seven, and_1_out, and_2_out);
  or or_2 (outstate[1], and_4_out, and_5_out);
  or or_3 (outstate[0], and_6_out, and_7_out, and_8_out);
endmodule

module EightLogic (
  input  [7:0] char,
  input  [2:0] instate,
  output eight,
  output [2:0] outstate
);

  wire and_1_out, and_2_out, and_4_out, and_5_out, and_6_out, and_7_out, and_8_out, not_1_out, not_2_out,
       not_3_out, not_4_out, not_5_out, not_6_out, not_7_out, not_8_out, not_9_out, not_10_out;

  not not_1 (not_1_out, char[7]);
  not not_2 (not_2_out, char[6]);
  not not_3 (not_3_out, char[4]);
  not not_4 (not_4_out, char[3]);
  not not_5 (not_5_out, char[2]);
  not not_6 (not_6_out, char[1]);
  not not_7 (not_7_out, char[0]);
  not not_8 (not_8_out, instate[2]);
  not not_9 (not_9_out, instate[1]);
  not not_10 (not_10_out, instate[0]);
  and and_1 (and_1_out, not_1_out, not_2_out, char[5], char[4], char[3], not_5_out, not_6_out, not_7_out);
  and and_2 (and_2_out, not_1_out, char[6], char[5], char[4], not_4_out, char[2], not_6_out, not_7_out, instate[2], not_9_out, not_10_out);
  and and_3 (outstate[2], not_1_out, char[6], char[5], not_3_out, char[3], not_5_out, not_6_out, not_7_out, not_8_out, instate[1], instate[0]);
  and and_4 (and_4_out, not_1_out, char[6], char[5], not_3_out, char[3], not_5_out, not_6_out, char[0], not_8_out, not_9_out, instate[0]);
  and and_5 (and_5_out, not_1_out, char[6], char[5], not_3_out, not_4_out, char[2], char[1], char[0], not_8_out, instate[1], not_10_out);
  and and_6 (and_6_out, not_1_out, char[6], char[5], not_3_out, not_4_out, char[2], not_6_out, char[0], not_8_out);
  and and_7 (and_7_out, not_1_out, char[6], char[5], not_3_out, not_4_out, char[2], char[0], not_8_out, instate[1], not_10_out);
  and and_8 (and_8_out, not_1_out, char[6], char[5], not_3_out, not_4_out, char[2], not_6_out, char[0], not_9_out, not_10_out);
  or or_1 (eight, and_1_out, and_2_out);
  or or_2 (outstate[1], and_4_out, and_5_out);
  or or_3 (outstate[0], and_6_out, and_7_out, and_8_out);
endmodule

module NineLogic (
  input  [7:0] char,
  input  [1:0] instate,
  output nine,
  output [1:0] outstate
);

  wire and_1_out, and_2_out, and_3_out, and_4_out, not_1_out, not_2_out, not_3_out, not_4_out, not_5_out,
       not_6_out, not_7_out, not_8_out, not_9_out;

  not not_1 (not_1_out, char[7]);
  not not_2 (not_2_out, char[6]);
  not not_3 (not_3_out, char[4]);
  not not_4 (not_4_out, char[3]);
  not not_5 (not_5_out, char[2]);
  not not_6 (not_6_out, char[1]);
  not not_7 (not_7_out, char[0]);
  not not_8 (not_8_out, instate[1]);
  not not_9 (not_9_out, instate[0]);
  and and_1 (and_1_out, not_1_out, not_2_out, char[5], char[4], char[3], not_5_out, not_6_out, char[0]);
  and and_2 (and_2_out, not_1_out, char[6], char[5], not_3_out, not_4_out, char[2], not_6_out, char[0], instate[1], instate[0]);
  and and_3 (and_3_out, not_1_out, char[6], char[5], not_3_out, char[3], not_5_out, not_6_out, char[0], not_8_out, instate[0]);
  and and_4 (and_4_out, not_1_out, char[6], char[5], not_3_out, char[3], char[2], char[1], not_7_out, instate[1], not_9_out);
  and and_5 (outstate[0], not_1_out, char[6], char[5], not_3_out, char[3], char[2], char[1], not_7_out);
  or or_1 (nine, and_1_out, and_2_out);
  or or_2 (outstate[1], and_3_out, and_4_out);
endmodule

module ZeroFSM (
  input  [7:0] char,
  input  clock,
  output zero
);

  wire [1:0] register_1_q, zerologic_1_outstate;

  Register #(.width(2)) register_1 (.D(zerologic_1_outstate), .clk(clock), .Q(register_1_q));  // open: en, clr
  ZeroLogic zerologic_1 (.char(char), .instate(register_1_q), .zero(zero), .outstate(zerologic_1_outstate));
endmodule

module OneFSM (
  input  [7:0] char,
  input  clock,
  output one
);

  wire [1:0] onelogic_1_outstate, register_1_q;

  Register #(.width(2)) register_1 (.D(onelogic_1_outstate), .clk(clock), .Q(register_1_q));  // open: en, clr
  OneLogic onelogic_1 (.char(char), .instate(register_1_q), .one(one), .outstate(onelogic_1_outstate));
endmodule

module TwoFSM (
  input  [7:0] char,
  input  clock,
  output two
);

  wire [1:0] register_1_q, twologic_1_outstate;

  Register #(.width(2)) register_1 (.D(twologic_1_outstate), .clk(clock), .Q(register_1_q));  // open: en, clr
  TwoLogic twologic_1 (.char(char), .instate(register_1_q), .two(two), .outstate(twologic_1_outstate));
endmodule

module ThreeFSM (
  input  [7:0] char,
  input  clock,
  output three
);

  wire [2:0] register_1_q, threelogic_1_outstate;

  Register #(.width(3)) register_1 (.D(threelogic_1_outstate), .clk(clock), .Q(register_1_q));  // open: en, clr
  ThreeLogic threelogic_1 (.char(char), .instate(register_1_q), .three(three), .outstate(threelogic_1_outstate));
endmodule

module FourFSM (
  input  [7:0] char,
  input  clock,
  output four
);

  wire [1:0] fourlogic_1_outstate, register_1_q;

  Register #(.width(2)) register_1 (.D(fourlogic_1_outstate), .clk(clock), .Q(register_1_q));  // open: en, clr
  FourLogic fourlogic_1 (.char(char), .instate(register_1_q), .four(four), .outstate(fourlogic_1_outstate));
endmodule

module FiveFSM (
  input  [7:0] char,
  input  clock,
  output five
);

  wire [1:0] fivelogic_1_outstate, register_1_q;

  Register #(.width(2)) register_1 (.D(fivelogic_1_outstate), .clk(clock), .Q(register_1_q));  // open: en, clr
  FiveLogic fivelogic_1 (.char(char), .instate(register_1_q), .five(five), .outstate(fivelogic_1_outstate));
endmodule

module SixFSM (
  input  [7:0] char,
  input  clock,
  output six
);

  wire [1:0] register_1_q, sixlogic_1_outstate;

  Register #(.width(2)) register_1 (.D(sixlogic_1_outstate), .clk(clock), .Q(register_1_q));  // open: en, clr
  SixLogic sixlogic_1 (.char(char), .instate(register_1_q), .six(six), .outstate(sixlogic_1_outstate));
endmodule

module SevenFSM (
  input  [7:0] char,
  input  clock,
  output seven
);

  wire [2:0] register_1_q, sevenlogic_1_outstate;

  Register #(.width(3)) register_1 (.D(sevenlogic_1_outstate), .clk(clock), .Q(register_1_q));  // open: en, clr
  SevenLogic sevenlogic_1 (.char(char), .instate(register_1_q), .seven(seven), .outstate(sevenlogic_1_outstate));
endmodule

module EightFSM (
  input  [7:0] char,
  input  clock,
  output eight
);

  wire [2:0] eightlogic_1_outstate, register_1_q;

  Register #(.width(3)) register_1 (.D(eightlogic_1_outstate), .clk(clock), .Q(register_1_q));  // open: en, clr
  EightLogic eightlogic_1 (.char(char), .instate(register_1_q), .eight(eight), .outstate(eightlogic_1_outstate));
endmodule

module NineFSM (
  input  [7:0] char,
  input  clock,
  output nine
);

  wire [1:0] ninelogic_1_outstate, register_1_q;

  Register #(.width(2)) register_1 (.D(ninelogic_1_outstate), .clk(clock), .Q(register_1_q));  // open: en, clr
  NineLogic ninelogic_1 (.char(char), .instate(register_1_q), .nine(nine), .outstate(ninelogic_1_outstate));
endmodule
